# Fritzing sketch bits-ldr-sample-fritzing-file (saved by Fritzing 0.9.3b)
circuit board: 8.46667cm x 5.64444cm
breadboards: 1

parts:
  Part1 = Arduino Uno (Rev3) - ICSP
  R1 = PHOTOCELL [package=photocell-kit]
  R2 = Resistor [tolerance=±5% resistance=1k package="0603 [SMD]"]

nets:
  N1: Part1.A0, R1.P$1, R2.Pin_1
  N2: Part1.5V, R2.Pin_0
  N3: Part1.GND, R1.P$2
