# Fritzing sketch dht11sensorrpi (saved by Fritzing 0.9.3b)
breadboards: 1

parts:
  Raspberry_Pi_1 = Raspberry Pi 3 [part_number=RPI-3-V1.2]
  DHT1 = DHT11 Humitidy and Temperature Sensor

nets:
  GND: Raspberry_Pi_1.GND, DHT1.GND
  N1: Raspberry_Pi_1.GIPO21, DHT1.DATA
  5V: Raspberry_Pi_1.5V, DHT1.VDD

custom parts:
  DHT11 Humitidy and Temperature Sensor: DHT11 Humidity and Temperature Sensor
