# Fritzing sketch rpi-led-interfacing (saved by Fritzing 0.9.3b)
circuit board: 8.46667cm x 5.64444cm
breadboards: 1

parts:
  Raspberry_Pi_1 = Raspberry Pi 3 [part_number=RPI-3-V1.2]
  LED1 = LED - 3mm [color="Red (633nm)" package="3 mm [THT]"]
  R1 = Resistor [tolerance=±5% resistance=330 package="0603 [SMD]"]
  LED2 = smd LED [color="Red (633nm)" package="0603 [SMD]"]
  R2 = Resistor [tolerance=±5% resistance=330 package="0805 [SMD]"]

nets:
  N1: Raspberry_Pi_1.GND, LED2.cathode
  N2: Raspberry_Pi_1.GIPO21, LED1.cathode
  N3: Raspberry_Pi_1.GIPO20, R2.Pin_1
  N4: Raspberry_Pi_1.5V, R1.Pin_1
  N5: LED1.anode, R1.Pin_0
  N6: LED2.anode, R2.Pin_0
